# Fritzing sketch Design (saved by Fritzing 0.9.3b)
breadboards: 1

parts:
  Part1 = Arduino Nano (Rev3.0)
  LED1 = LED - 5mm [color="Red (633nm)" package="5 mm [THT]"]
  S2 = Pushbutton [package=THT]
  S3 = Pushbutton [package="[THT]"]
  R2 = Resistor [tolerance=±5% resistance=220 package=THT]
  SPKR1 = Loudspeaker
  S4 = Pushbutton [package="[THT]"]
  R3 = Resistor [tolerance=±5% resistance=220 package=THT]
  U1 = RELAY [package=relay-t9a-2]
  R4 = Resistor [tolerance=±5% resistance=220 package=THT]

nets:
  N1: Part1.D10, U1.COIL2
  N2: Part1.D11/MOSI, S4.Pin_3, S4.Pin_4, R3.Pin_0
  N3: Part1.D12/MISO, S3.Pin_3
  N4: Part1.VIN, S3.Pin_1, S3.Pin_2, S4.Pin_1, S4.Pin_2
  N5: Part1.GND, LED1.cathode, S2.leg1, R2.Pin_1, R3.Pin_1, U1.COIL1
  N6: LED1.anode, R4.Pin_1
  N7: S2.leg0, SPKR1.pin1
  N8: SPKR1.pin2, U1.NO, R4.Pin_0
